# Fritzing sketch Progetto03 (saved by Fritzing 0.9.3b)
breadboards: 1

parts:
  Componente2 = Arduino Uno (Rev3)
  LED3 = smd LED [color="Green (555nm)" package="0603 [SMD]"]
  LED4 = smd LED [color="Red (633nm)" package="0603 [SMD]"]
  LED5 = smd LED [color="Green (555nm)" package="0603 [SMD]"]
  R5 = Resistor [tolerance=±5% resistance=220 package="2010 [SMD]"]
  R6 = Resistor [tolerance=±5% resistance=220 package="2010 [SMD]"]
  R7 = Resistor [tolerance=±5% resistance=220 package="2010 [SMD]"]
  hc-sr2 = hc-sr04
  J1 = Basic Servo
  Componente3 = Bluetooth HC-05 Macho
  U2 = ESP8266 WiFi Module [part_number=ESP8266]
  R8 = Rotary Potentiometer (Small) [maximum_resistance=100kΩ package=THT]

nets:
  N1: Componente2.D8, hc-sr2.Trig
  N2: Componente2.D10_PWM/SS, J1.pulse
  N3: Componente2.D2, Componente3.TXD
  N4: Componente2.D3_PWM, Componente3.RXD
  N5: Componente2.D4, R5.Pin_1
  N6: Componente2.D5_PWM, R6.Pin_1
  N7: Componente2.D6_PWM, R7.Pin_1
  N8: Componente2.D7, hc-sr2.Echo
  VCC: Componente2.5V, hc-sr2.VCC, J1.vcc, Componente3.VCC
  GND: Componente2.GND, LED3.cathode, LED4.cathode, LED5.cathode, hc-sr2.GND, J1.gnd, Componente3.GND
  N9: LED3.anode, R5.Pin_0
  N10: LED4.anode, R6.Pin_0
  N11: LED5.anode, R7.Pin_0
  N12: U2.VCC, R8.leg2
  N13: U2.GND, R8.leg1
  N14: U2.ADC_0, R8.wiper
