# Fritzing sketch schema (saved by Fritzing 0.9.3b)
breadboards: 1

parts:
  Part1 = Arduino Uno (Rev3)
  R1 = Resistor [tolerance=±5% resistance=220 package=THT]
  LED1 = LED - 5mm [color="Green (560nm)" package="5 mm [THT]"]
  T2 = Pushbutton [package="[THT]"]
  R2 = Resistor [tolerance=±5% resistance=10k package=THT]
  L3 = LED - 5mm [color="Green (560nm)" package="5 mm [THT]"]
  R3 = Resistor [tolerance=±5% resistance=220 package=THT]
  L1 = LED - 5mm [color="Green (560nm)" package="5 mm [THT]"]
  R4 = Resistor [tolerance=±5% resistance=220 package=THT]
  T1 = Pushbutton [package="[THT]"]
  R6 = Resistor [tolerance=±5% resistance=10k package=THT]
  LED_FLASH = LED - 5mm [color="Red (660nm)" package="5 mm [THT]"]
  R7 = Resistor [tolerance=±5% resistance=220 package=THT]
  POT = Rotary Potentiometer (Small) [maximum_resistance=100kΩ package=THT]
  T3 = Pushbutton [package="[THT]"]
  R9 = Resistor [tolerance=±5% resistance=10k package=THT]

nets:
  N1: Part1.A0, POT.wiper
  N2: Part1.D8, R4.Pin_1
  N3: Part1.D9_PWM, R3.Pin_1
  N4: Part1.D10_PWM/SS, R7.Pin_1
  N5: Part1.D2, T1.Pin_3, T1.Pin_4, R6.Pin_1
  N6: Part1.D3_PWM, T2.Pin_3, T2.Pin_4, R2.Pin_1
  N7: Part1.D4, T3.Pin_3, T3.Pin_4, R9.Pin_1
  N8: Part1.D7, R1.Pin_1
  N9: Part1.5V, T2.Pin_1, T2.Pin_2, T1.Pin_1, T1.Pin_2, POT.leg2, T3.Pin_1, T3.Pin_2
  N10: Part1.GND, LED1.cathode, R2.Pin_0, L1.cathode, R6.Pin_0, LED_FLASH.cathode, POT.leg1, R9.Pin_0
  N11: R1.Pin_0, L1.anode
  N12: LED1.anode, R3.Pin_0
  N13: L3.anode, R4.Pin_0
  N14: LED_FLASH.anode, R7.Pin_0
